// Logisim project ALU_starter.circ as structural Verilog: 9 circuits, main circuit main
module main (
  input  [31:0] IN1,
  input  [31:0] IN2,
  input  [2:0] SEL,
  output [31:0] OUT
);

  ALU alu_1 (.Input1(IN1), .Input2(IN2), .Sel(SEL), .Output(OUT));
endmodule

module ALU (
  input  [31:0] Input1,
  input  [31:0] Input2,
  input  [2:0] Sel,
  output [31:0] Output
);

  wire [31:0] and_1_out, or_1_out, rl_1_out_3, rr_1_out_3, sll_1_out_3, sra_1_out_3, srl_1_out_3, xor_1_out_3;

  sll sll_1 (.in_1(Input1), .in_2(Input2), .out_3(sll_1_out_3));
  srl srl_1 (.in_1(Input1), .in_2(Input2), .out_3(srl_1_out_3));
  sra sra_1 (.in_1(Input1), .in_2(Input2), .out_3(sra_1_out_3));
  rl rl_1 (.in_1(Input1), .in_2(Input2), .out_3(rl_1_out_3));
  rr rr_1 (.in_1(Input1), .in_2(Input2), .out_3(rr_1_out_3));
  assign and_1_out = Input1 & Input2;  // AND_Gate and_1, 32 bits wide
  assign or_1_out = Input1 | Input2;  // OR_Gate or_1, 32 bits wide
  \xor  xor_1 (.in_1(Input2), .in_2(Input1), .out_3(xor_1_out_3));
  Multiplexer #(.select(3), .width(32)) multiplexer_1 (
    .in0(sll_1_out_3), .in1(srl_1_out_3), .in2(sra_1_out_3), .in3(rl_1_out_3), .in4(rr_1_out_3),
    .in5(and_1_out), .in6(or_1_out), .in7(xor_1_out_3), .out(Output), .sel(Sel));  // open: en
endmodule

module sll (
  input  [31:0] in_1,
  input  [31:0] in_2,
  output [31:0] out_3
);

  Shifter #(.width(32)) shifter_1 (.in(in_1), .\dist (in_2[4:0]), .out(out_3));
endmodule

module srl (
  input  [31:0] in_1,
  input  [31:0] in_2,
  output [31:0] out_3
);

  Shifter #(.width(32), .shift("lr")) shifter_1 (.in(in_1), .\dist (in_2[4:0]), .out(out_3));
endmodule

module sra (
  input  [31:0] in_1,
  input  [31:0] in_2,
  output [31:0] out_3
);

  Shifter #(.width(32), .shift("ar")) shifter_1 (.in(in_1), .\dist (in_2[4:0]), .out(out_3));
endmodule

module rl (
  input  [31:0] in_1,
  input  [31:0] in_2,
  output [31:0] out_3
);

  Shifter #(.width(32), .shift("rl")) shifter_1 (.in(in_1), .\dist (in_2[4:0]), .out(out_3));
endmodule

module rr (
  input  [31:0] in_1,
  input  [31:0] in_2,
  output [31:0] out_3
);

  Shifter #(.width(32), .shift("rr")) shifter_1 (.in(in_1), .\dist (in_2[4:0]), .out(out_3));
endmodule

module \xor  (
  input  [31:0] in_1,
  input  [31:0] in_2,
  output [31:0] out_3
);

  wire [31:0] and_1_out, and_2_out, not_1_out, not_2_out;

  assign not_1_out = ~in_1;  // NOT_Gate not_1, 32 bits wide
  assign not_2_out = ~in_2;  // NOT_Gate not_2, 32 bits wide
  assign and_1_out = in_1 & not_2_out;  // AND_Gate and_1, 32 bits wide
  assign and_2_out = not_1_out & in_2;  // AND_Gate and_2, 32 bits wide
  assign out_3 = and_1_out | and_2_out;  // OR_Gate or_1, 32 bits wide
endmodule

module test (
  input  [31:0] in_1,
  input  [4:0] in_2,
  output [31:0] out_3
);

  Shifter #(.width(32)) shifter_1 (.in(in_1), .\dist (in_2), .out(out_3));
endmodule
