// Logisim project fib15.circ as structural Verilog: 2 circuits, main circuit main
module main (
  output [9:0] out_1
);

  wire clock_1_out, register_3_q;
  wire [9:0] initialize_1_out_2, register_1_q, register_2_q;

  Register #(.width(10)) register_1 (.D(out_1), .Q(register_1_q), .clk(clock_1_out));  // open: en, clr
  Clock clock_1 (.out(clock_1_out));
  initialize initialize_1 (.in_1(register_1_q), .out_2(initialize_1_out_2));
  Adder #(.width(10)) adder_1 (.a(register_1_q), .b(register_2_q), .out(out_1));  // open: cin, cout
  Register #(.width(10)) register_2 (
    .D(initialize_1_out_2), .Q(register_2_q), .clk(clock_1_out), .clr(register_3_q));  // open: en
  Register #(.width(1)) register_3 (.D(out_1[9]), .Q(register_3_q), .clk(clock_1_out));  // open: en, clr
endmodule

module initialize (
  input  [9:0] in_1,
  output [9:0] out_2
);

  wire not_1_out, or_1_out;

  Multiplexer #(.width(10)) multiplexer_1 (.in0(in_1), .in1(10'h1), .out(out_2), .sel(not_1_out));  // open: en
  or or_1 (or_1_out, in_1[0], in_1[1], in_1[2], in_1[3], in_1[4], in_1[6], in_1[7], in_1[8], in_1[9], in_1[5]);
  not not_1 (not_1_out, or_1_out);
endmodule
