// Logisim project shift.circ as structural Verilog: 7 circuits, main circuit main
module main (
  input  [15:0] in_1,
  input  [3:0] in_2,
  output [15:0] out_3
);

  wire n1_or_not_1_out_2, n1_or_not_2_out_2, n1_or_not_3_out_2, n1_or_not_4_out_2;
  wire [15:0] shift1_1_out_4, shift2_1_out_4, shift4_1_out_4;

  _1_or_not u_1_or_not_1 (.in_1(in_2[0]), .out_2(n1_or_not_1_out_2));
  shift1 shift1_1 (.in_1(in_1), .in_2(n1_or_not_1_out_2), .in_3(in_1), .out_4(shift1_1_out_4));
  _1_or_not u_1_or_not_2 (.in_1(in_2[1]), .out_2(n1_or_not_2_out_2));
  shift2 shift2_1 (.in_1(shift1_1_out_4), .in_2(n1_or_not_2_out_2), .in_3(shift1_1_out_4), .out_4(shift2_1_out_4));
  _1_or_not u_1_or_not_3 (.in_1(in_2[2]), .out_2(n1_or_not_3_out_2));
  shift4 shift4_1 (.in_1(shift2_1_out_4), .in_2(n1_or_not_3_out_2), .in_3(shift2_1_out_4), .out_4(shift4_1_out_4));
  _1_or_not u_1_or_not_4 (.in_1(in_2[3]), .out_2(n1_or_not_4_out_2));
  shift8 shift8_1 (.in_1(shift4_1_out_4), .in_2(n1_or_not_4_out_2), .in_3(shift4_1_out_4), .out_4(out_3));
endmodule

module _1_or_not (
  input  in_1,
  output out_2
);

  and and_1 (out_2, in_1, 1'b1);
endmodule

module shift1 (
  input  [15:0] in_1,
  input  in_2,
  input  [15:0] in_3,
  output [15:0] out_4
);

  wire not_1_out;
  wire [15:0] and_1_out, and_2_out, n1to16_1_out_2, n1to16_2_out_2;

  _1to16 u_1to16_1 (.in_1(in_2), .out_2(n1to16_1_out_2));
  not not_1 (not_1_out, in_2);
  _1to16 u_1to16_2 (.in_1(not_1_out), .out_2(n1to16_2_out_2));
  assign and_1_out = {in_1[0], in_1[15:1]} & {in_1[0], in_1[15:1]} & n1to16_1_out_2;  // AND_Gate and_1, 16 bits wide
  assign and_2_out = n1to16_2_out_2 & in_3;  // AND_Gate and_2, 16 bits wide
  assign out_4 = and_1_out | and_2_out;  // OR_Gate or_1, 16 bits wide
endmodule

module _1to16 (
  input  in_1,
  output [15:0] out_2
);


  assign out_2 = {16{in_1}};
endmodule

module shift2 (
  input  [15:0] in_1,
  input  in_2,
  input  [15:0] in_3,
  output [15:0] out_4
);

  wire not_1_out;
  wire [15:0] and_1_out, and_2_out, n1to16_1_out_2, n1to16_2_out_2;

  _1to16 u_1to16_1 (.in_1(in_2), .out_2(n1to16_1_out_2));
  not not_1 (not_1_out, in_2);
  _1to16 u_1to16_2 (.in_1(not_1_out), .out_2(n1to16_2_out_2));
  assign and_1_out = {in_1[1:0], in_1[15:2]} & {in_1[1:0], in_1[15:2]} & n1to16_1_out_2;  // AND_Gate and_1, 16 bits wide
  assign and_2_out = n1to16_2_out_2 & in_3;  // AND_Gate and_2, 16 bits wide
  assign out_4 = and_1_out | and_2_out;  // OR_Gate or_1, 16 bits wide
endmodule

module shift4 (
  input  [15:0] in_1,
  input  in_2,
  input  [15:0] in_3,
  output [15:0] out_4
);

  wire not_1_out;
  wire [15:0] and_1_out, and_2_out, n1to16_1_out_2, n1to16_2_out_2;

  _1to16 u_1to16_1 (.in_1(in_2), .out_2(n1to16_1_out_2));
  _1to16 u_1to16_2 (.in_1(not_1_out), .out_2(n1to16_2_out_2));
  not not_1 (not_1_out, in_2);
  assign and_1_out = {in_1[3:0], in_1[15:4]} & {in_1[3:0], in_1[15:4]} & n1to16_1_out_2;  // AND_Gate and_1, 16 bits wide
  assign and_2_out = n1to16_2_out_2 & in_3;  // AND_Gate and_2, 16 bits wide
  assign out_4 = and_1_out | and_2_out;  // OR_Gate or_1, 16 bits wide
endmodule

module shift8 (
  input  [15:0] in_1,
  input  in_2,
  input  [15:0] in_3,
  output [15:0] out_4
);

  wire not_1_out;
  wire [15:0] and_1_out, and_2_out, n1to16_1_out_2, n1to16_2_out_2;

  _1to16 u_1to16_1 (.in_1(in_2), .out_2(n1to16_1_out_2));
  not not_1 (not_1_out, in_2);
  _1to16 u_1to16_2 (.in_1(not_1_out), .out_2(n1to16_2_out_2));
  assign and_1_out = {in_1[7:0], in_1[15:8]} & {in_1[7:0], in_1[15:8]} & n1to16_1_out_2;  // AND_Gate and_1, 16 bits wide
  assign and_2_out = n1to16_2_out_2 & in_3;  // AND_Gate and_2, 16 bits wide
  assign out_4 = and_1_out | and_2_out;  // OR_Gate or_1, 16 bits wide
endmodule
